# Fritzing sketch BiltongMasterLayout (saved by Fritzing 1.0.2b)
circuit board: 11cm x 6.5cm
breadboards: 1

parts:
  CLK = ESP32-38PinWide [part_number=ESP32-38PinWide]
  FAN = Header 4 [package=molex-1x4_lock]
  Sense = Header 3 [package=molex-1x3_lock]
  IC1 = ULN2003A [package="DIP16 [THT]"]
  J1 = Power Jack [package=power_jack_slot]
  U1 = Voltage Regulator - 5V [package="TO220 [THT]"]
  U2 = RELAY [package=relay-g5q]
  MAIN = Camdenboss CTB0158-3 [part_number=CTB0158-3 package=THT]
  BULB = Camdenboss CTB0158-3 [part_number=CTB0158-3 package=THT]
  F1 = FUSE [package=fuse_5mm]

nets:
  N1: CLK.3.3, Sense.3
  GND: CLK.GND, FAN.1, Sense.1, IC1.0V, J1.GNDBREAK, J1.GND, U1.GND
  N2: CLK.VIN, U1.output_voltage
  N3: CLK.GPIO16, FAN.4
  N4: CLK.GPIO17, FAN.3
  N5: CLK.GPIO18, IC1.In_7
  N6: CLK.GPIO23, Sense.2
  N7: FAN.2, IC1.COM_-_Common, J1.PWR, U1.input_voltage, U2.COIL2
  N8: IC1.Out_7, U2.COIL1
  N9: U2.MAIN, F1.2
  N10: U2.NO, BULB.pin1
  N11: MAIN.pin1, BULB.pin3
  N12: MAIN.pin2, BULB.pin2
  N13: MAIN.pin3, F1.1

notes:
  ULN2003A
  BILTONG MAKER V1
  by YOKOMAFOODS.COM
  OUT L7805CV IN

custom parts:
  ESP32-38PinWide: Generic 38-Pin ESP32 with wide format (only access to one side of pins on a breadboard) based on Stephen Lilley's HiLetgo ESP-WROOM-32 ESP32 ESP-32S Development Board.
